// Logisim project miniCurso.circ as structural Verilog: 3 circuits, main circuit main
module main (
  input  A,
  input  B,
  input  carry_in,
  input  in_4,
  input  in_5,
  input  in_6,
  input  A_2,
  input  B_2,
  output carry_out,
  output Soma_Final,
  output out_11,
  output carry_out_final,
  output out_13,
  output out_14,
  output Soma_Final_2,
  output Cin,
  output SomaAB
);

  wire halfadder_1_cin, halfadder_1_somaab, halfadder_2_cin;

  FullAdder fulladder_1 (
    .A(in_4), .B(in_5), .carry_in(in_6), .carry_out1(out_11), .carry_out_final(carry_out_final), .S1(out_13),
    .carry_out2(out_14), .S(Soma_Final_2));
  HalfAdder halfadder_1 (.A(A), .B(B), .Cin(halfadder_1_cin), .SomaAB(halfadder_1_somaab));
  or or_1 (Soma_Final, halfadder_1_cin, halfadder_2_cin);
  HalfAdder halfadder_2 (.A(halfadder_1_somaab), .B(carry_in), .Cin(halfadder_2_cin), .SomaAB(carry_out));
  and and_1 (Cin, A_2, B_2);
  xor xor_1 (SomaAB, A_2, B_2);
endmodule

module HalfAdder (
  input  A,
  input  B,
  output Cin,
  output SomaAB
);

  and and_1 (Cin, A, B);
  xor xor_1 (SomaAB, A, B);
endmodule

module FullAdder (
  input  A,
  input  B,
  input  carry_in,
  output carry_out1,
  output carry_out_final,
  output S1,
  output carry_out2,
  output S
);

  and and_1 (carry_out1, A, B);
  xor xor_1 (S1, A, B);
  xor xor_2 (S, S1, carry_in);
  and and_2 (carry_out2, S1, carry_in);
  or or_1 (carry_out_final, carry_out1, carry_out2);
endmodule
